# Fritzing sketch TILMotherboard (saved by Fritzing 0.9.3b)

parts:
  U1 = MAX485 [package=dil08]
  U2 = ESP32S-HiLetgo [part_number=ESP32S-HiLetgo]
  U3 = OpenMV3
  XLR1 = XLR3_NCFAH2 [package=xlr3_nc3fah2]

nets:
  N1: U1.DE, U1.VCC, U2.3.3
  N2: U1.DI, U2.GPIO2
  GND: U1.GND, U2.GND, U3.GND, XLR1.1
  N3: U1.A, XLR1.3
  N4: U1.B, XLR1.2
  N5: U2.GPIO12, U3.P4/TX3/SCL
  VIN: U2.VIN, U3.VIN

notes:
  DMX Output
  Camera Input

custom parts:
  ESP32S-HiLetgo: HiLetgo ESP-WROOM-32 ESP32 ESP-32S Development Board 2.4GHz Dual-Mode WiFi + Bluetooth Dual Cores Microcontroller The ESP32 integrated with Antenna switches, RF Balun, power amplifiers, low-noise amplifiers, filters, and management modules, and the entire solution occupies the least area of PCB. 2.4 GHz Wi-Fi plus Bluetooth dual-mode chip, with TSMC Ultra-low power consumption 40nm technology,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
  OpenMV3: OpenMV Cam
